# Fritzing sketch Sketch (saved by Fritzing 0.9.3b)
breadboards: 1

parts:
  Part1 = Arduino Uno (Rev3)
  LCD1 = LCD screen
  U1 = POT [package=pot_mammoth]
  hc-sr1 = hc-sr04

nets:
  N1: Part1.D9_PWM, LCD1.E
  N2: Part1.D10_PWM/SS, LCD1.RS
  N3: Part1.D11_PWM/MOSI, hc-sr1.Echo
  N4: Part1.D13/SCK, hc-sr1.Trig
  GND: Part1.GND, LCD1.VSS, LCD1.R/W, LCD1.LED-, U1.S, hc-sr1.GND
  N5: Part1.D2, LCD1.DB7
  N6: Part1.D3_PWM, LCD1.DB6
  N7: Part1.D4, LCD1.DB5
  N8: Part1.D5_PWM, LCD1.DB4
  5V: Part1.5V, LCD1.VDD, LCD1.LED+, U1.E, hc-sr1.VCC
  N9: LCD1.V0, U1.A
