# Fritzing sketch Untitled Sketch (saved by Fritzing 0.9.3b)
breadboards: 1

parts:
  Part1 = Arduino Uno (Rev3)
  U1 = AD22100 - Voltage Output Temperature Sensor with Signal Conditioning [part_number=AD22100]
  LCD1 = LCD screen

nets:
  N1: Part1.A0, U1.Vo
  N2: Part1.D11_PWM/MOSI, LCD1.E
  N3: Part1.D12/MISO, LCD1.RS
  N4: Part1.D2, LCD1.DB7
  N5: Part1.D3_PWM, LCD1.DB6
  N6: Part1.D4, LCD1.DB5
  N7: Part1.D5_PWM, LCD1.DB4
  5V: Part1.5V, U1.V+, LCD1.VDD, LCD1.LED+
  GND: Part1.GND, U1.GND, LCD1.VSS, LCD1.V0, LCD1.R/W, LCD1.LED-
